# Fritzing sketch BeeHive (saved by Fritzing 1.0.8)
stripboards: 2

parts:
  A4 = ina226 module
  U1 = LIPO-2000mAh [package=lipo-2000]
  A5 = CN3065 Mini Solar Charger Module
  D1 = SOLAR-IXYS [package=solarbit-12x1]
  Adafruit_NAU7802_Breakout_Rev_C1 = Adafruit NAU7802 Breakout Rev C [mn=Adafruit mpn=#4538 part_number=#4538]
  A6 = featherS3
  Part1 = INMP441
  U2 = SHT40 Breakout [mn=Sensirion package="Breakout Module [THT]"]

nets:
  N1: A4.Pin_1, D1.A
  N2: A4.Pin_2, A4.Pin_3, A5.Pin_1
  N3: A4.Pin_5, Adafruit_NAU7802_Breakout_Rev_C1.SCL, A6.Pin_22, U2.SCL
  N4: A4.Pin_6, Adafruit_NAU7802_Breakout_Rev_C1.SDA, A6.Pin_21, U2.SDA
  GND: A4.Pin_7, A4.Pin_9, A4.Pin_11, U1.-, A5.Pin_2, A5.Pin_8, A5.Pin_10, D1.C, Adafruit_NAU7802_Breakout_Rev_C1.GND, A6.Pin_4, A6.Pin_17, Part1.L/R, Part1.GND, U2.GND
  VCC: A4.Pin_8, A4.Pin_10, Adafruit_NAU7802_Breakout_Rev_C1.VCC, A6.Pin_16, Part1.VDD, U2.VIN
  N5: U1.+, A5.Pin_7, A5.Pin_9, A6.Pin_32
  N6: A6.Pin_25, Part1.WS
  N7: A6.Pin_26, Part1.SCK
  N8: A6.Pin_27, Part1.SD

custom parts:
  ina226 module: INA226 Voltage Current/Power Monitoring Sensor Module IIC I2C Interface Bi-directional INA226 Module CJMCU-226.
  CN3065 Mini Solar Charger Module: Fc-51 Infrared Obstacle Avoidance Proximity Sensor module. IR transmitter led, receiver LED, lm393 compaitor and a pot. 3.3 V to 5V power.
  featherS3: FeatherS3 is the latest in our super popular ESP32 based Feather boards.
  INMP441: This is a simple breakout board for the INMP441 I2S MEMS microphone.
  SHT40 Breakout: SHT40 Temperature and Humidity Sensor Breakout Module. Sensirion SHT40 with I2C interface (address 0x44). 10mm x 13mm purple PCB with 4-pin header (VIN, GND, SCL, SDA).
